// Logisim project controle.circ as structural Verilog: 1 circuit, main circuit controle
module controle (
  input  [5:0] INSTR_CLASS,
  input  CLK,
  input  RESET,
  input  DF,
  input  Q_IN,
  input  [3:0] EF,
  input  D_ZERO,
  output [2:0] NEXT_STATE,
  output COND_EN,
  output Q_LOAD,
  output DF_LOAD,
  output REG_DEC,
  output REG_INC,
  output IR_LOAD,
  output MEM_WR,
  output MEM_RD,
  output [3:0] REG_SEL,
  output [2:0] ADDR_SRC,
  output [3:0] DST,
  output [2:0] SRC_B,
  output [2:0] SRC_A,
  output [3:0] ALU_OP,
  output [2:0] ESTADO
);

  Register #(.width(3)) REG_ESTADO (.D(NEXT_STATE), .clk(CLK), .Q(ESTADO), .clr(RESET));  // open: en
  ROM #(.addrWidth(9), .dataWidth(32)) uROM (.addr({ESTADO, INSTR_CLASS}));  // open: data
endmodule
